// Logisim project MIPS32.circ as structural Verilog
module main (
);

  wire as1, control_1_p3, control_1_p5, control_1_p7, control_1_p9, data_1_p5, ex2mem_1_p2, ex2mem_1_p5, h1,
       mem2wb_1_p7, MemRead, MemWrite, RegDst, RegisterFile_p7, RegisterFile_p8, RWF, undriven, Write;
  wire [1:0] ForwardA, ForwardB;
  wire [4:0] ex2mem_1_p4, h2, RegDSTF, rtypeinstructionsplitter_1_rd, rtypeinstructionsplitter_1_rs,
       rtypeinstructionsplitter_1_rt, rtypeinstructionsplitter_2_rs, rtypeinstructionsplitter_2_rt,
       rtypeinstructionsplitter_2_shamt;
  wire [5:0] ALUop, id2ex_1_p24, rtypeinstructionsplitter_1_opcode, rtypeinstructionsplitter_2_func;
  wire [10:0] alucontrol_1_alufunc;
  wire [15:0] if2id_1_ins, if2id_1_ins_2;
  wire [31:0] adder_1_out, adder_3_out, alu_1_result, ex2mem_1_p3, EXMNextPC_q, id2ex_1_p21, id2ex_1_p22,
       if2id_1_npc, instructions_1_instruction, it1, mem2wb_1_p3, mem2wb_1_p4, multiplexer_5_out,
       multiplexer_6_out, multiplexer_8_out, PC_q, register_1_q, RegisterFile_p4, s2, shifter_2_out,
       signextend_1_value_u32;

  Multiplexer #(.width(32)) multiplexer_1 (.in0(adder_1_out), .in1(EXMNextPC_q));  // open: out, sel
  Register #(.width(32)) PC (.Q(PC_q));  // open: D, en, clk, clr
  Adder #(.width(32)) adder_1 (.a(PC_q), .b(32'h4), .out(adder_1_out));  // open: cin, cout
  Instructions instructions_1 (.Read(PC_q), .Instruction(instructions_1_instruction));
  // CLKmodul clkmodul_1: pin names not known
  IF2ID if2id_1 (
    .PCin(adder_1_out), .InsIn(instructions_1_instruction), .NPC(if2id_1_npc),
    .Ins({if2id_1_ins_2, if2id_1_ins}));  // open: en
  RtypeInstructionSplitter rtypeinstructionsplitter_1 (
    .Instruction({if2id_1_ins_2, if2id_1_ins}), .Opcode(rtypeinstructionsplitter_1_opcode),
    .Rs(rtypeinstructionsplitter_1_rs), .Rt(rtypeinstructionsplitter_1_rt), .Rd(rtypeinstructionsplitter_1_rd));  // open: shamt, func
  Multiplexer #(.width(5)) multiplexer_2 ();  // open: in0, in1, out, sel
  Shifter #(.width(32)) shifter_1 (.\dist (5'b00010));  // open: in, out
  HazardDetectionUnit hazarddetectionunit_1 (
    .IDEXMemRead(h1), .IFIDRegRs(rtypeinstructionsplitter_1_rs), .IDEXRegRt(h2),
    .IFIDRegRt(rtypeinstructionsplitter_1_rt));  // open: stall, IFIDWrite
  SignExtend signextend_1 (.Value_u16(if2id_1_ins), .Value_u32(signextend_1_value_u32));
  // Registers RegisterFile: pin names not known; wires that end beside it: rtypeinstructionsplitter_1_rs, rtypeinstructionsplitter_1_rt, RegDSTF, RegisterFile_p4, RWF, if2id_1_npc, RegisterFile_p7, RegisterFile_p8
  Adder #(.width(32)) adder_2 ();  // open: a, b, out, cin, cout
  // Control control_1: pin names not known; wires that end beside it: rtypeinstructionsplitter_1_opcode, RegDst, control_1_p3, MemRead, control_1_p5, MemWrite, control_1_p7, Write, control_1_p9, ALUop
  Multiplexer #(.width(32)) multiplexer_3 ();  // open: in0, in1, out, sel
  Multiplexer #(.width(32)) multiplexer_4 ();  // open: in0, in1, out, sel
  // AND_Gate and_1 is placed but not wired
  Register #(.width(32)) register_1 (.D(if2id_1_npc), .Q(register_1_q));  // open: en, clk, clr
  // ID2EX id2ex_1: pin names not known; wires that end beside it: {if2id_1_ins_2, if2id_1_ins}, RegisterFile_p7, RegisterFile_p8, signextend_1_value_u32, ALUop, control_1_p7, RegDst, control_1_p3, MemWrite, MemRead, Write, control_1_p5, rtypeinstructionsplitter_1_rt, rtypeinstructionsplitter_1_rs, rtypeinstructionsplitter_1_rd, control_1_p9, control_1_p9, control_1_p9, control_1_p9, it1, id2ex_1_p21, id2ex_1_p22, s2, id2ex_1_p24, as1, h1, h2
  RtypeInstructionSplitter rtypeinstructionsplitter_2 (
    .Instruction(it1), .Rs(rtypeinstructionsplitter_2_rs), .Rt(rtypeinstructionsplitter_2_rt),
    .shamt(rtypeinstructionsplitter_2_shamt), .func(rtypeinstructionsplitter_2_func));  // open: Opcode, Rd
  Multiplexer #(.select(2), .width(32)) multiplexer_5 (
    .in0(id2ex_1_p22), .in1(RegisterFile_p4), .in2(ex2mem_1_p3), .out(multiplexer_5_out), .sel(ForwardB));  // open: in3
  Multiplexer #(.select(2), .width(32)) multiplexer_6 (
    .in0(id2ex_1_p21), .in1(RegisterFile_p4), .in2(ex2mem_1_p3), .out(multiplexer_6_out), .sel(ForwardA));  // open: in3
  Multiplexer #(.width(32)) multiplexer_7 (.sel(undriven));  // open: in0, in1, out
  Shifter #(.width(32)) shifter_2 (.in(s2), .\dist (5'b00010), .out(shifter_2_out));
  Multiplexer #(.width(32)) multiplexer_8 (.in0(multiplexer_5_out), .in1(s2), .out(multiplexer_8_out), .sel(as1));
  Adder #(.width(32)) adder_3 (.a(register_1_q), .b(shifter_2_out), .out(adder_3_out));  // open: cin, cout
  ALUControl alucontrol_1 (
    .SHAMT(rtypeinstructionsplitter_2_shamt), .ALUop(id2ex_1_p24), .Func(rtypeinstructionsplitter_2_func),
    .ALUFunc(alucontrol_1_alufunc));
  ForwardUnit forwardunit_1 (
    .EXMrd(ex2mem_1_p4), .MWBrd(RegDSTF), .IDEXrs(rtypeinstructionsplitter_2_rs),
    .IDEXrt(rtypeinstructionsplitter_2_rt), .EXMregwrite(ex2mem_1_p5), .MWBregwrite(RWF),
    .ForwardA(ForwardA), .ForwardB(ForwardB));
  // SignExtend signextend_2: pin names not known
  ALU alu_1 (
    .Operand1(multiplexer_6_out), .Operand2(multiplexer_8_out), .ALUfunc(alucontrol_1_alufunc),
    .Result(alu_1_result));  // open: ZF
  Register #(.width(32)) EXMNextPC (.D(adder_3_out), .Q(EXMNextPC_q));  // open: en, clk, clr
  // EX2MEM ex2mem_1: pin names not known; wires that end beside it: alu_1_result, ex2mem_1_p2, ex2mem_1_p3, ex2mem_1_p4, ex2mem_1_p5
  // Data data_1: pin names not known; wires that end beside it: ex2mem_1_p2, MemWrite, MemRead, ex2mem_1_p3, data_1_p5
  // MEM2WB mem2wb_1: pin names not known; wires that end beside it: ex2mem_1_p3, data_1_p5, mem2wb_1_p3, mem2wb_1_p4, RegDSTF, RWF, mem2wb_1_p7
  Multiplexer #(.width(32)) multiplexer_9 (
    .in0(mem2wb_1_p3), .in1(mem2wb_1_p4), .out(RegisterFile_p4), .sel(mem2wb_1_p7));
endmodule

module Registers (
  input  CLK,
  input  [4:0] ReadRegister1,
  input  [4:0] ReadRegister2,
  input  [4:0] WriteRegister,
  input  [31:0] WriteData,
  input  Write,
  input  PCtoReg31,
  input  [31:0] PC,
  output [31:0] ReadData1,
  output [31:0] ReadData2
);

  wire decoder_1_out0, decoder_1_out1, decoder_1_out2, decoder_1_out3, decoder_1_out4, decoder_1_out5,
       decoder_1_out6, decoder_1_out7, decoder_1_out8, decoder_1_out9, decoder_1_out10, decoder_1_out11,
       decoder_1_out12, decoder_1_out13, decoder_1_out14, decoder_1_out15, decoder_1_out16, decoder_1_out17,
       decoder_1_out18, decoder_1_out19, decoder_1_out20, decoder_1_out21, decoder_1_out22, decoder_1_out23,
       decoder_1_out24, decoder_1_out25, decoder_1_out26, decoder_1_out27, decoder_1_out28, decoder_1_out29,
       decoder_1_out30, decoder_1_out31;
  wire [31:0] multiplexer_1_out, register_1_q, register_2_q, register_3_q, register_4_q, register_5_q,
       register_6_q, register_7_q, register_8_q, register_9_q, register_10_q, register_11_q, register_12_q,
       register_13_q, register_14_q, register_15_q, register_16_q, register_17_q, register_18_q,
       register_19_q, register_20_q, register_21_q, register_22_q, register_23_q, register_24_q,
       register_25_q, register_26_q, register_27_q, register_28_q, register_29_q, register_30_q,
       register_31_q, register_32_q;

  Decoder #(.select(5)) decoder_1 (
    .out0(decoder_1_out0), .out1(decoder_1_out1), .out2(decoder_1_out2), .out3(decoder_1_out3),
    .out4(decoder_1_out4), .out5(decoder_1_out5), .out6(decoder_1_out6), .out7(decoder_1_out7),
    .out8(decoder_1_out8), .out9(decoder_1_out9), .out10(decoder_1_out10), .out11(decoder_1_out11),
    .out12(decoder_1_out12), .out13(decoder_1_out13), .out14(decoder_1_out14), .out15(decoder_1_out15),
    .out16(decoder_1_out16), .out17(decoder_1_out17), .out18(decoder_1_out18), .out19(decoder_1_out19),
    .out20(decoder_1_out20), .out21(decoder_1_out21), .out22(decoder_1_out22), .out23(decoder_1_out23),
    .out24(decoder_1_out24), .out25(decoder_1_out25), .out26(decoder_1_out26), .out27(decoder_1_out27),
    .out28(decoder_1_out28), .out29(decoder_1_out29), .out30(decoder_1_out30), .out31(decoder_1_out31),
    .sel(WriteRegister), .en(Write));
  Multiplexer #(.width(32)) multiplexer_1 (.in0(WriteData), .in1(PC), .out(multiplexer_1_out), .sel(PCtoReg31));
  Register #(.width(32)) register_1 (.D(WriteData), .en(decoder_1_out0), .clk(CLK), .Q(register_1_q));  // open: clr
  Register #(.width(32)) register_2 (
    .D(WriteData), .en(decoder_1_out1), .clk(decoder_1_out0), .Q(register_2_q));  // open: clr
  Register #(.width(32)) register_3 (
    .D(WriteData), .en(decoder_1_out2), .clk(decoder_1_out0), .Q(register_3_q));  // open: clr
  Register #(.width(32)) register_4 (
    .D(WriteData), .en(decoder_1_out3), .clk(decoder_1_out0), .Q(register_4_q));  // open: clr
  Register #(.width(32)) register_5 (
    .D(WriteData), .en(decoder_1_out4), .clk(decoder_1_out0), .Q(register_5_q));  // open: clr
  Register #(.width(32)) register_6 (
    .D(WriteData), .en(decoder_1_out5), .clk(decoder_1_out0), .Q(register_6_q));  // open: clr
  Register #(.width(32)) register_7 (
    .D(WriteData), .en(decoder_1_out6), .clk(decoder_1_out0), .Q(register_7_q));  // open: clr
  Register #(.width(32)) register_8 (
    .D(WriteData), .en(decoder_1_out7), .clk(decoder_1_out0), .Q(register_8_q));  // open: clr
  Register #(.width(32)) register_9 (
    .D(WriteData), .en(decoder_1_out8), .clk(decoder_1_out0), .Q(register_9_q));  // open: clr
  Register #(.width(32)) register_10 (
    .D(WriteData), .en(decoder_1_out9), .clk(decoder_1_out0), .Q(register_10_q));  // open: clr
  Register #(.width(32)) register_11 (
    .D(WriteData), .en(decoder_1_out10), .clk(decoder_1_out0), .Q(register_11_q));  // open: clr
  Register #(.width(32)) register_12 (
    .D(WriteData), .en(decoder_1_out11), .clk(decoder_1_out0), .Q(register_12_q));  // open: clr
  Register #(.width(32)) register_13 (
    .D(WriteData), .en(decoder_1_out12), .clk(decoder_1_out0), .Q(register_13_q));  // open: clr
  Register #(.width(32)) register_14 (
    .D(WriteData), .en(decoder_1_out13), .clk(decoder_1_out0), .Q(register_14_q));  // open: clr
  Register #(.width(32)) register_15 (
    .D(WriteData), .en(decoder_1_out14), .clk(decoder_1_out0), .Q(register_15_q));  // open: clr
  Register #(.width(32)) register_16 (
    .D(WriteData), .en(decoder_1_out15), .clk(decoder_1_out0), .Q(register_16_q));  // open: clr
  Register #(.width(32)) register_17 (
    .D(WriteData), .en(decoder_1_out16), .clk(decoder_1_out0), .Q(register_17_q));  // open: clr
  Register #(.width(32)) register_18 (
    .D(WriteData), .en(decoder_1_out17), .clk(decoder_1_out0), .Q(register_18_q));  // open: clr
  Register #(.width(32)) register_19 (
    .D(WriteData), .en(decoder_1_out18), .clk(decoder_1_out0), .Q(register_19_q));  // open: clr
  Register #(.width(32)) register_20 (
    .D(WriteData), .en(decoder_1_out19), .clk(decoder_1_out0), .Q(register_20_q));  // open: clr
  Register #(.width(32)) register_21 (
    .D(WriteData), .en(decoder_1_out20), .clk(decoder_1_out0), .Q(register_21_q));  // open: clr
  Register #(.width(32)) register_22 (
    .D(WriteData), .en(decoder_1_out21), .clk(decoder_1_out0), .Q(register_22_q));  // open: clr
  Register #(.width(32)) register_23 (
    .D(WriteData), .en(decoder_1_out22), .clk(decoder_1_out0), .Q(register_23_q));  // open: clr
  Register #(.width(32)) register_24 (
    .D(WriteData), .en(decoder_1_out23), .clk(decoder_1_out0), .Q(register_24_q));  // open: clr
  Register #(.width(32)) register_25 (
    .D(WriteData), .en(decoder_1_out24), .clk(decoder_1_out0), .Q(register_25_q));  // open: clr
  Register #(.width(32)) register_26 (
    .D(WriteData), .en(decoder_1_out25), .clk(decoder_1_out0), .Q(register_26_q));  // open: clr
  Register #(.width(32)) register_27 (
    .D(WriteData), .en(decoder_1_out26), .clk(decoder_1_out0), .Q(register_27_q));  // open: clr
  Register #(.width(32)) register_28 (
    .D(WriteData), .en(decoder_1_out27), .clk(decoder_1_out0), .Q(register_28_q));  // open: clr
  Register #(.width(32)) register_29 (
    .D(WriteData), .en(decoder_1_out28), .clk(decoder_1_out0), .Q(register_29_q));  // open: clr
  Register #(.width(32)) register_30 (
    .D(WriteData), .en(decoder_1_out29), .clk(decoder_1_out0), .Q(register_30_q));  // open: clr
  Register #(.width(32)) register_31 (
    .D(WriteData), .en(decoder_1_out30), .clk(decoder_1_out0), .Q(register_31_q));  // open: clr
  Register #(.width(32)) register_32 (
    .D(multiplexer_1_out), .en(decoder_1_out31), .clk(decoder_1_out0), .Q(register_32_q));  // open: clr
  Multiplexer #(.select(5), .width(32)) multiplexer_2 (
    .in0(register_1_q), .in1(register_2_q), .in2(register_3_q), .in3(register_4_q), .in4(register_5_q),
    .in5(register_6_q), .in6(register_7_q), .in7(register_8_q), .in8(register_9_q), .in9(register_10_q),
    .in10(register_11_q), .in11(register_12_q), .in12(register_13_q), .in13(register_14_q),
    .in14(register_15_q), .in15(register_16_q), .in16(register_17_q), .in17(register_18_q),
    .in18(register_19_q), .in19(register_20_q), .in20(register_21_q), .in21(register_22_q),
    .in22(register_23_q), .in23(register_24_q), .in24(register_25_q), .in25(register_26_q),
    .in26(register_27_q), .in27(register_28_q), .in28(register_29_q), .in29(register_30_q),
    .in30(register_31_q), .in31(register_32_q), .out(ReadData1), .sel(ReadRegister1));
  Multiplexer #(.select(5), .width(32)) multiplexer_3 (
    .in0(register_1_q), .in1(register_2_q), .in2(register_3_q), .in3(register_4_q), .in4(register_5_q),
    .in5(register_6_q), .in6(register_7_q), .in7(register_8_q), .in8(register_9_q), .in9(register_10_q),
    .in10(register_11_q), .in11(register_12_q), .in12(register_13_q), .in13(register_14_q),
    .in14(register_15_q), .in15(register_16_q), .in16(register_17_q), .in17(register_18_q),
    .in18(register_19_q), .in19(register_20_q), .in20(register_21_q), .in21(register_22_q),
    .in22(register_23_q), .in23(register_24_q), .in24(register_25_q), .in25(register_26_q),
    .in26(register_27_q), .in27(register_28_q), .in28(register_29_q), .in29(register_30_q),
    .in30(register_31_q), .in31(register_32_q), .out(ReadData2), .sel(ReadRegister2));

  // Other names for the same wires on the sheet: WD[31:0] = WriteData
endmodule

module ALU (
  input  [31:0] Operand1,
  input  [31:0] Operand2,
  input  [10:0] ALUfunc,
  output ZF,
  output [31:0] Result
);

  wire [31:0] Add, aright, BAnd, bnor, bor, bxor, logleft, logright, lui, multiplexer_1_out,
       multiplexer_2_out, shifter_1_out, slt, sub;

  Shifter #(.width(32)) shifter_1 (.in(Operand2), .\dist (5'b01111), .out(shifter_1_out));
  Shifter shifter_2 ();  // open: in, dist, out
  Shifter #(.width(32)) shifter_3 (.in(Operand1), .\dist (ALUfunc[4:0]), .out(logleft));
  Shifter #(.shift("lr"), .width(32)) shifter_4 (.in(Operand1), .\dist (ALUfunc[4:0]), .out(logright));
  Shifter #(.shift("ar"), .width(32)) shifter_5 (.in(Operand1), .\dist (ALUfunc[4:0]), .out(aright));
  Shifter #(.shift("rl"), .width(32)) shifter_6 (.in(Operand1), .\dist (ALUfunc[4:0]));  // open: out
  Shifter #(.shift("rr"), .width(32)) shifter_7 (.in(Operand1), .\dist (ALUfunc[4:0]));  // open: out
  Adder #(.width(32)) adder_1 (.a(Operand1), .b(Operand2), .out(Add));  // open: cin, cout
  Subtractor #(.width(32)) subtractor_1 (.a(Operand1), .b(Operand2), .out(sub));  // open: bin, bout
  assign BAnd = Operand1 & Operand2;  // AND_Gate and_1, 32 bits wide
  assign bor = Operand1 | Operand2;  // OR_Gate or_1, 32 bits wide
  // NOT_Gate not_1 has open pins: in=Operand1, out=open
  assign bxor = Operand1 ^ Operand2;  // XOR_Gate xor_1, 32 bits wide
  Negator #(.width(32)) negator_1 (.in(Operand1));  // open: out
  sltkolo sltkolo_1 (.operand1(Operand1), .operand2(Operand2), .out_3(slt));
  Adder #(.width(32)) adder_2 (.a(Operand1), .b(shifter_1_out), .out(lui));  // open: cin, cout
  Adder adder_3 ();  // open: a, b, out, cin, cout
  assign bnor = ~bor;  // NOT_Gate not_2, 32 bits wide
  Multiplexer #(.select(5), .width(32)) multiplexer_1 (
    .in0(logleft), .in2(logright), .in3(aright), .in8(Operand1), .in17(lui), .out(multiplexer_1_out),
    .sel(ALUfunc[9:5]));  // open: in1, in4, in5, in6, in7, in9, in10, in11, in12, in13, in14, in15, in16, in18, in19, in20, in21, in22, in23, in24, in25, in26, in27, in28, in29, in30, in31
  Multiplexer #(.select(5), .width(32)) multiplexer_2 (
    .in0(Add), .in2(sub), .in4(BAnd), .in5(bor), .in6(bxor), .in7(bnor), .in10(slt), .out(multiplexer_2_out));  // open: in1, in3, in8, in9, in11, in12, in13, in14, in15, in16, in17, in18, in19, in20, in21, in22, in23, in24, in25, in26, in27, in28, in29, in30, in31, sel
  Multiplexer #(.width(32)) multiplexer_3 (
    .in0(multiplexer_1_out), .in1(multiplexer_2_out), .out(Result), .sel(ALUfunc[10]));
  and and_2 (ZF, ~Result[0], ~Result[1], ~Result[2], ~Result[3], ~Result[4], ~Result[5], ~Result[6], ~Result[7], ~Result[8], ~Result[9], ~Result[10], ~Result[11], ~Result[12], ~Result[13], ~Result[14], ~Result[15], ~Result[17], ~Result[18], ~Result[19], ~Result[20], ~Result[21], ~Result[22], ~Result[23], ~Result[24], ~Result[25], ~Result[26], ~Result[27], ~Result[28], ~Result[29], ~Result[30], ~Result[31], ~Result[16]);  // AND_Gate

  // Other names for the same wires on the sheet: allpass[31:0] = Operand1; LS[4:0] = ALUfunc[9:5]; HS = ALUfunc[10]

  // Notes on the sheet:
  //   velicina?
endmodule

module Data (
  input  CLK,
  input  [31:0] Address,
  input  MemWrite,
  input  MemRead,
  input  [31:0] WriteData,
  input  [1:0] Mode,
  output [31:0] ReadData
);

  wire [7:0] multiplexer_2_out, ram_1_dout, ram_2_dout, ram_3_dout, ram_4_dout;
  wire [15:0] multiplexer_1_out;
  wire [31:0] signextend_1_value_u32, signextendbyte_1_a32;

  RAM ram_1 (.addr(Address[7:0]), .we(MemWrite), .oe(MemRead), .clk(CLK), .din(WriteData[7:0]), .dout(ram_1_dout));
  RAM ram_2 (.addr(Address[15:8]), .we(MemWrite), .oe(MemRead), .clk(CLK), .din(WriteData[15:8]), .dout(ram_2_dout));
  RAM ram_3 (.addr(Address[23:16]), .we(MemWrite), .oe(MemRead), .clk(CLK), .din(WriteData[23:16]), .dout(ram_3_dout));
  RAM ram_4 (.addr(Address[31:24]), .we(MemWrite), .oe(MemRead), .clk(CLK), .din(WriteData[31:24]), .dout(ram_4_dout));
  Multiplexer #(.width(16)) multiplexer_1 (
    .in0({ram_2_dout, ram_1_dout}), .out(multiplexer_1_out), .sel(Address[1]));  // open: in1
  Multiplexer #(.select(2), .width(8)) multiplexer_2 (
    .in0(ram_1_dout), .in1(ram_2_dout), .in2(ram_3_dout), .in3(ram_4_dout), .out(multiplexer_2_out),
    .sel(Address[1:0]));
  SignExtend signextend_1 (.Value_u16(multiplexer_1_out), .Value_u32(signextend_1_value_u32));
  SignExtendByte signextendbyte_1 (.a(multiplexer_2_out), .a32(signextendbyte_1_a32));
  Multiplexer #(.select(2), .width(32)) multiplexer_3 (
    .in0({ram_4_dout, ram_3_dout, ram_2_dout, ram_1_dout}), .in1(signextend_1_value_u32),
    .in2(signextendbyte_1_a32), .out(ReadData), .sel(Mode));  // open: in3
endmodule

module Instructions (
  input  [31:0] Read,
  output [31:0] Instruction
);

  ROM #(.addrWidth(16), .dataWidth(32)) rom_1 (.addr(Read[15:0]), .data(Instruction));
endmodule

module SignExtend (
  input  [15:0] Value_u16,
  output [31:0] Value_u32
);


  assign Value_u32 = {{17{Value_u16[15]}}, Value_u16[14:0]};
endmodule

module Control (
  input  [5:0] Opcode,
  output RegDst,
  output Branch,
  output MemRead,
  output MemToReg,
  output MemWrite,
  output ALUSrc,
  output RegWrite,
  output [1:0] AdrMode,
  output [5:0] ALUop,
  output RegToPC
);

  wire [4:4] rom_1_data;

  ROM #(.addrWidth(6)) rom_1 (
    .addr(Opcode), .data({RegWrite, ALUSrc, MemWrite, rom_1_data[4], MemToReg, MemRead, Branch, RegDst}));
  ROM #(.addrWidth(6), .dataWidth(6)) rom_2 (.addr(Opcode), .data(ALUop));

  // Notes on the sheet:
  //   contents of rom_1 (hex, n*v repeats v):
  //   0 0 4*42 0 0 3 0 3 0 3 3 0 1 16*0 33 0 0 33 4*0 6 0 0 6
  //   contents of rom_2 (hex, n*v repeats v):
  //   3f 0 0 0 22 22 0 0 20 0 2a 0 24 25 0 11 16*0 20 0 0 20 4*0 20 0 0 20
endmodule

module ALUControl (
  input  [4:0] SHAMT,
  input  [5:0] ALUop,
  input  [5:0] Func,
  output [10:0] ALUFunc
);

  wire and_1_out;

  Multiplexer #(.width(6)) multiplexer_1 (.in0(ALUop), .in1(Func), .out(ALUFunc[10:5]), .sel(and_1_out));
  and and_1 (and_1_out, ALUop[0], ALUop[1], ALUop[2], ALUop[4], ALUop[5], ALUop[3]);

  assign ALUFunc[4:0] = SHAMT;
endmodule

module sltkolo (
  input  [31:0] operand1,
  input  [31:0] operand2,
  output [31:0] out_3
);

  wire [30:0] subtractor_1_out;

  Subtractor #(.width(32)) subtractor_1 (
    .a(operand1), .b(operand2), .out({out_3[0], subtractor_1_out}));  // open: bin, bout

  assign out_3[31:1] = {31{1'b0}};
endmodule

module CLKmodul (
  input  CLK,
  input  RST,
  output phase0,
  output phase90
);

  wire d_ff_1_qn, d_ff_2_qn, not_1_out;

  D_Flip_Flop d_ff_1 (.D(d_ff_1_qn), .clk(CLK), .Q(phase0), .Qn(d_ff_1_qn), .reset(RST));  // open: preset
  D_Flip_Flop d_ff_2 (.D(d_ff_2_qn), .clk(not_1_out), .Q(phase90), .Qn(d_ff_2_qn), .reset(RST));  // open: preset
  not not_1 (not_1_out, CLK);
endmodule

module IF2ID (
  input  [31:0] PCin,
  input  [31:0] InsIn,
  input  en,
  output [31:0] NPC,
  output [31:0] Ins
);

  Register #(.width(32)) NextPC (.D(PCin), .en(en), .Q(NPC));  // open: clk, clr
  Register #(.width(32)) Instruction (.D(InsIn), .en(en), .Q(Ins));  // open: clk, clr
endmodule

module ID2EX (
  input  flush,
  input  CLK,
  input  [31:0] NPC,
  input  [31:0] InsIn,
  input  [31:0] OP1in,
  input  [31:0] OP2in,
  input  [31:0] SEin,
  input  [4:0] RegDstIn,
  input  [5:0] ALUOPIN,
  input  ALUSrcIN,
  input  RegDstMUXin,
  input  BranchIn,
  input  MemWriteIn,
  input  MemReadIn,
  input  RegWriteIn,
  input  MemToRegIn,
  input  [4:0] rtin,
  input  [4:0] rsin,
  input  [4:0] rdin,
  input  [1:0] AdrMode,
  output [31:0] NextPC,
  output [31:0] Ins,
  output [31:0] OP1out,
  output [31:0] OP2out,
  output [31:0] SEout,
  output [4:0] RegDstOut,
  output [5:0] ALUOPOUT,
  output ALUSrcOut,
  output RegDstMUXout,
  output BranchOut,
  output MemWriteOut,
  output MemReadOut,
  output RegWriteOut,
  output MemToRegOut,
  output [4:0] rtout,
  output [4:0] rsout,
  output [4:0] rdout,
  output [1:0] Mode
);

  wire multiplexer_7_out, multiplexer_8_out, multiplexer_9_out, multiplexer_10_out, multiplexer_11_out,
       multiplexer_12_out, multiplexer_13_out;
  wire [1:0] multiplexer_16_out;
  wire [4:0] multiplexer_5_out, multiplexer_14_out, multiplexer_15_out, multiplexer_18_out;
  wire [5:0] multiplexer_6_out;
  wire [31:0] multiplexer_1_out, multiplexer_2_out, multiplexer_3_out, multiplexer_4_out, multiplexer_17_out;

  Multiplexer #(.width(32)) multiplexer_1 (.in0(NPC), .in1({32{1'b0}}), .out(multiplexer_1_out), .sel(flush));
  Multiplexer #(.width(32)) multiplexer_2 (.in0(InsIn), .in1({32{1'b0}}), .out(multiplexer_2_out), .sel(flush));
  Multiplexer #(.width(32)) multiplexer_3 (.in0(OP1in), .in1({32{1'b0}}), .out(multiplexer_3_out), .sel(flush));
  Multiplexer #(.width(32)) multiplexer_4 (.in0(OP2in), .in1({32{1'b0}}), .out(multiplexer_4_out), .sel(flush));
  Multiplexer #(.width(5)) multiplexer_5 (.in0(RegDstIn), .in1({5{1'b0}}), .out(multiplexer_5_out), .sel(flush));
  Multiplexer #(.width(6)) multiplexer_6 (.in0(ALUOPIN), .in1({6{1'b0}}), .out(multiplexer_6_out), .sel(flush));
  Multiplexer multiplexer_7 (.in0(ALUSrcIN), .in1(1'b0), .out(multiplexer_7_out), .sel(flush));
  Multiplexer multiplexer_8 (.in0(RegDstMUXin), .in1(1'b0), .out(multiplexer_8_out), .sel(flush));
  Multiplexer multiplexer_9 (.in0(BranchIn), .in1(1'b0), .out(multiplexer_9_out), .sel(flush));
  Multiplexer multiplexer_10 (.in0(MemWriteIn), .in1(1'b0), .out(multiplexer_10_out), .sel(flush));
  Multiplexer multiplexer_11 (.in0(MemReadIn), .in1(1'b0), .out(multiplexer_11_out), .sel(flush));
  Multiplexer multiplexer_12 (.in0(RegWriteIn), .in1(1'b0), .out(multiplexer_12_out), .sel(flush));
  Multiplexer multiplexer_13 (.in0(MemToRegIn), .in1(1'b0), .out(multiplexer_13_out), .sel(flush));
  Multiplexer #(.width(5)) multiplexer_14 (.in0(rtin), .in1({5{1'b0}}), .out(multiplexer_14_out), .sel(flush));
  Multiplexer #(.width(5)) multiplexer_15 (.in0(rsin), .in1({5{1'b0}}), .out(multiplexer_15_out), .sel(flush));
  Multiplexer #(.width(2)) multiplexer_16 (.in0(AdrMode), .in1(2'b00), .out(multiplexer_16_out), .sel(flush));
  Multiplexer #(.width(32)) multiplexer_17 (.in0(SEin), .in1({32{1'b0}}), .out(multiplexer_17_out), .sel(flush));
  Multiplexer #(.width(5)) multiplexer_18 (.in0(rdin), .in1({5{1'b0}}), .out(multiplexer_18_out), .sel(flush));
  Register #(.width(32)) register_1 (.D(multiplexer_1_out), .en(1'b1), .clk(CLK), .Q(NextPC));  // open: clr
  Register #(.width(32)) Instruction (.D(multiplexer_2_out), .en(1'b1), .clk(CLK), .Q(Ins));  // open: clr
  Register #(.width(32)) Operand1 (.D(multiplexer_3_out), .en(1'b1), .clk(CLK), .Q(OP1out));  // open: clr
  Register #(.width(32)) Operand2 (.D(multiplexer_4_out), .en(1'b1), .clk(CLK), .Q(OP2out));  // open: clr
  Register #(.width(32)) SignExtend (.D(multiplexer_17_out), .en(1'b1), .clk(CLK), .Q(SEout));  // open: clr
  Register #(.width(5)) Destination (.D(multiplexer_5_out), .en(1'b1), .clk(CLK), .Q(RegDstOut));  // open: clr
  Register #(.width(6)) ALUOP (.D(multiplexer_6_out), .en(1'b1), .clk(CLK), .Q(ALUOPOUT));  // open: clr
  D_Flip_Flop RegDstSignal (.D(multiplexer_8_out), .clk(CLK), .Q(RegDstMUXout));  // open: Qn, preset, reset
  D_Flip_Flop Branch (.D(multiplexer_9_out), .clk(CLK), .Q(BranchOut));  // open: Qn, preset, reset
  D_Flip_Flop MemWrite (.D(multiplexer_10_out), .clk(CLK), .Q(MemWriteOut));  // open: Qn, preset, reset
  D_Flip_Flop RegWrite (.D(multiplexer_12_out), .clk(CLK), .Q(RegWriteOut));  // open: Qn, preset, reset
  D_Flip_Flop MemToReg (.D(multiplexer_13_out), .clk(CLK), .Q(MemToRegOut));  // open: Qn, preset, reset
  D_Flip_Flop ALUSrc (.D(multiplexer_7_out), .clk(CLK), .Q(ALUSrcOut));  // open: Qn, preset, reset
  D_Flip_Flop MemRead (.D(multiplexer_11_out), .clk(CLK), .Q(MemReadOut));  // open: Qn, preset, reset
  Register #(.width(5)) Rt (.D(multiplexer_14_out), .en(1'b1), .clk(CLK), .Q(rtout));  // open: clr
  Register #(.width(5)) Rs (.D(multiplexer_15_out), .en(1'b1), .clk(CLK), .Q(rsout));  // open: clr
  Register #(.width(5)) Rd (.D(multiplexer_18_out), .en(1'b1), .clk(CLK), .Q(rdout));  // open: clr
  Register #(.width(2)) register_2 (.D(multiplexer_16_out), .en(1'b1), .clk(CLK), .Q(Mode));  // open: clr

  // Notes on the sheet:
  //   EX GRUPA
  //   M Grupa
  //   W Grupa
endmodule

module EX2MEM (
  input  Flush,
  input  CLK,
  input  [31:0] NPC,
  input  [31:0] AddrIn,
  input  [31:0] ResultIn,
  input  [31:0] RegIn,
  input  ZeroIn,
  input  [4:0] RegDstIn,
  input  BranchIn,
  input  MemWriteIn,
  input  MemReadIn,
  input  [1:0] AdrMode,
  input  RegWriteIn,
  input  MemToRegIn,
  output [31:0] NextPC,
  output [31:0] AddrOut,
  output [31:0] ResultOut,
  output [31:0] RegOut,
  output ZeroOut,
  output [4:0] RegDstOut,
  output BranchOut,
  output MemWriteOut,
  output MemReadOut,
  output [1:0] Mode,
  output RegWriteOut,
  output MemToRegOut
);

  wire multiplexer_4_out, multiplexer_7_out, multiplexer_8_out, multiplexer_9_out, multiplexer_10_out,
       multiplexer_11_out;
  wire [4:0] multiplexer_5_out;
  wire [31:0] multiplexer_1_out, multiplexer_2_out, multiplexer_3_out, multiplexer_6_out;

  Multiplexer #(.width(32)) multiplexer_1 (.in0(AddrIn), .in1({32{1'b0}}), .out(multiplexer_1_out), .sel(Flush));
  Multiplexer #(.width(32)) multiplexer_2 (.in0(ResultIn), .in1({32{1'b0}}), .out(multiplexer_2_out), .sel(Flush));
  Multiplexer #(.width(32)) multiplexer_3 (.in0(RegIn), .in1({32{1'b0}}), .out(multiplexer_3_out), .sel(Flush));
  Multiplexer multiplexer_4 (.in0(ZeroIn), .in1(1'b0), .out(multiplexer_4_out), .sel(Flush));
  Multiplexer #(.width(5)) multiplexer_5 (.in0(RegDstIn), .in1({5{1'b0}}), .out(multiplexer_5_out), .sel(Flush));
  Multiplexer #(.width(32)) multiplexer_6 (.in0(NPC), .in1({32{1'b0}}), .out(multiplexer_6_out), .sel(Flush));
  Multiplexer multiplexer_7 (.in0(BranchIn), .in1(1'b0), .out(multiplexer_7_out));  // open: sel
  Multiplexer multiplexer_8 (.in0(MemWriteIn), .in1(1'b0), .out(multiplexer_8_out));  // open: sel
  Multiplexer multiplexer_9 (.in0(MemReadIn), .in1(1'b0), .out(multiplexer_9_out), .sel(Flush));
  Multiplexer multiplexer_10 (.in0(RegWriteIn), .in1(1'b0), .out(multiplexer_10_out), .sel(Flush));
  Multiplexer multiplexer_11 (.in0(MemToRegIn), .in1(1'b0), .out(multiplexer_11_out), .sel(Flush));
  Register #(.width(32)) register_1 (.D(multiplexer_6_out), .en(1'b1), .clk(CLK), .Q(NextPC));  // open: clr
  Register #(.width(32)) BranchAddr (.D(multiplexer_1_out), .en(1'b1), .clk(CLK), .Q(AddrOut));  // open: clr
  Register #(.width(32)) Result (.D(multiplexer_2_out), .en(1'b1), .clk(CLK), .Q(ResultOut));  // open: clr
  Register #(.width(32)) RegisterFileRead (.D(multiplexer_3_out), .en(1'b1), .clk(CLK), .Q(RegOut));  // open: clr
  D_Flip_Flop ZeroFlag (.D(multiplexer_4_out), .clk(CLK), .Q(ZeroOut));  // open: Qn, preset, reset
  Register #(.width(5)) Destination (.D(multiplexer_5_out), .en(1'b1), .clk(CLK), .Q(RegDstOut));  // open: clr
  D_Flip_Flop Branch (.D(multiplexer_7_out), .clk(CLK), .Q(BranchOut));  // open: Qn, preset, reset
  D_Flip_Flop MemWrite (.D(multiplexer_8_out), .clk(CLK), .Q(MemWriteOut));  // open: Qn, preset, reset
  D_Flip_Flop MemRead (.D(multiplexer_9_out), .clk(CLK), .Q(MemReadOut));  // open: Qn, preset, reset
  D_Flip_Flop RegWrite (.D(multiplexer_10_out), .clk(CLK), .Q(RegWriteOut));  // open: Qn, preset, reset
  D_Flip_Flop MemToReg (.D(multiplexer_11_out), .clk(CLK), .Q(MemToRegOut));  // open: Qn, preset, reset
  Register #(.width(2)) register_2 (.D(AdrMode), .en(1'b1), .clk(CLK), .Q(Mode));  // open: clr

  // Notes on the sheet:
  //   M Grupa
  //   W Grupa
endmodule

module MEM2WB (
  input  CLK,
  input  [31:0] ResultIn,
  input  [31:0] DataIn,
  input  [4:0] RegDstIn,
  input  RegWriteIn,
  input  MemToRegIn,
  output [31:0] ResultOut,
  output [31:0] DataOut,
  output [4:0] RegDstOut,
  output RegWriteOut,
  output MemToRegOut
);

  Register #(.width(32)) Result (.D(ResultIn), .en(1'b1), .clk(CLK), .Q(ResultOut));  // open: clr
  Register #(.width(32)) Data (.D(DataIn), .en(1'b1), .clk(CLK), .Q(DataOut));  // open: clr
  Register #(.width(5)) Destination (.D(RegDstIn), .en(1'b1), .clk(CLK), .Q(RegDstOut));  // open: clr
  D_Flip_Flop RegWrite (.D(RegWriteIn), .clk(CLK), .Q(RegWriteOut));  // open: Qn, preset, reset
  D_Flip_Flop MemToReg (.D(MemToRegIn), .clk(CLK), .Q(MemToRegOut));  // open: Qn, preset, reset

  // Notes on the sheet:
  //   W Grupa
endmodule

module HazardDetectionUnit (
  input  IDEXMemRead,
  input  [4:0] IFIDRegRs,
  input  [4:0] IDEXRegRt,
  input  [4:0] IFIDRegRt,
  output stall,
  output IFIDWrite
);

  wire comparator5b_1_eq, comparator5b_2_eq, or_1_out;

  Comparator5b comparator5b_1 (.A(IFIDRegRs), .B(IDEXRegRt), .EQ(comparator5b_1_eq));
  Comparator5b comparator5b_2 (.A(IDEXRegRt), .B(IFIDRegRt), .EQ(comparator5b_2_eq));
  and and_1 (stall, IDEXMemRead, or_1_out);
  or or_1 (or_1_out, comparator5b_1_eq, comparator5b_2_eq);
endmodule

module Comparator5b (
  input  [4:0] A,
  input  [4:0] B,
  output EQ
);

  wire xor_1_out, xor_2_out, xor_3_out, xor_4_out, xor_5_out;

  xor xor_1 (xor_1_out, A[0], B[0]);
  xor xor_2 (xor_2_out, A[1], B[1]);
  xor xor_3 (xor_3_out, A[2], B[2]);
  xor xor_4 (xor_4_out, A[3], B[3]);
  xor xor_5 (xor_5_out, A[4], B[4]);
  and and_1 (EQ, ~xor_1_out, ~xor_2_out, ~xor_3_out, ~xor_4_out, ~xor_5_out);  // AND_Gate
endmodule

module RtypeInstructionSplitter (
  input  [31:0] Instruction,
  output [5:0] Opcode,
  output [4:0] Rs,
  output [4:0] Rt,
  output [4:0] Rd,
  output [4:0] shamt,
  output [5:0] func
);


  assign func = Instruction[5:0];
  assign Opcode = Instruction[31:26];
  assign Rd = Instruction[15:11];
  assign Rs = Instruction[25:21];
  assign Rt = Instruction[20:16];
  assign shamt = Instruction[10:6];
endmodule

module SignExtendByte (
  input  [7:0] a,
  output [31:0] a32
);


  assign a32 = {{25{a[7]}}, a[6:0]};
endmodule

module ForwardUnit (
  input  [4:0] EXMrd,
  input  [4:0] MWBrd,
  input  [4:0] IDEXrs,
  input  [4:0] IDEXrt,
  input  EXMregwrite,
  input  MWBregwrite,
  output [1:0] ForwardA,
  output [1:0] ForwardB
);

  wire comparator5b_1_eq, comparator5b_2_eq, comparator5b_3_eq, comparator5b_4_eq, comparator5b_5_eq,
       comparator5b_6_eq, comparator5b_7_eq, comparator5b_8_eq, not_1_out, not_2_out, not_3_out, not_4_out,
       not_5_out, not_6_out;

  Comparator5b comparator5b_1 (.A({5{1'b0}}), .B(EXMrd), .EQ(comparator5b_1_eq));
  Comparator5b comparator5b_2 (.A({5{1'b0}}), .B(MWBrd), .EQ(comparator5b_2_eq));
  Comparator5b comparator5b_3 (.A(MWBrd), .B(IDEXrs), .EQ(comparator5b_3_eq));
  not not_1 (not_1_out, comparator5b_1_eq);
  Comparator5b comparator5b_4 (.A(EXMrd), .B(IDEXrs), .EQ(comparator5b_4_eq));
  not not_2 (not_2_out, comparator5b_2_eq);
  and and_1 (ForwardA[1], not_1_out, EXMregwrite, comparator5b_4_eq);
  Comparator5b comparator5b_5 (.A({5{1'b0}}), .B(EXMrd), .EQ(comparator5b_5_eq));
  Comparator5b comparator5b_6 (.A({5{1'b0}}), .B(MWBrd), .EQ(comparator5b_6_eq));
  Comparator5b comparator5b_7 (.A(MWBrd), .B(IDEXrt), .EQ(comparator5b_7_eq));
  not not_3 (not_3_out, ForwardA[1]);
  not not_4 (not_4_out, comparator5b_5_eq);
  Comparator5b comparator5b_8 (.A(EXMrd), .B(IDEXrt), .EQ(comparator5b_8_eq));
  not not_5 (not_5_out, comparator5b_6_eq);
  and and_2 (ForwardA[0], not_3_out, not_2_out, comparator5b_3_eq, MWBregwrite);
  and and_3 (ForwardB[0], not_4_out, EXMregwrite, comparator5b_8_eq);
  not not_6 (not_6_out, ForwardB[0]);
  and and_4 (ForwardB[1], not_6_out, not_5_out, comparator5b_7_eq, MWBregwrite);
endmodule

module mips32 (
);

  wire EMreW, ex2mem_1_memreadout, ex2mem_1_memtoregout, ex2mem_1_memwriteout, iealusel, iedsel,
       mem2wb_1_memtoregout, MWregW, t2, t3, t4, t5, t6, zf;
  wire [1:0] ex2mem_1_mode, ForwardA, ForwardB, mde;
  wire [4:0] EMrd, ierd, IErs, IErt, MWrd, rdd, t1;
  wire [10:0] f;
  wire [31:0] alu_1_result, data_1_readdata, ex2mem_1_resultout, f01, f10, iea, ieb, ienpc, IEse,
       mem2wb_1_dataout, mem2wb_1_resultout, multiplexer_1_out, multiplexer_3_out, multiplexer_4_out;

  // HazardDetectionUnit hazarddetectionunit_1: pin names not known
  // SignExtend signextend_1: pin names not known
  Registers registers_1 ();  // open: CLK, ReadRegister1, ReadRegister2, WriteRegister, WriteData, Write, PCtoReg31, PC, ReadData1, ReadData2
  Control control_1 ();  // open: Opcode, RegDst, Branch, MemRead, MemToReg, MemWrite, ALUSrc, RegWrite, AdrMode, ALUop, RegToPC
  // ID2EX id2ex_1: pin names not known; wires that end beside it: ienpc, iea, ieb, IEse, t1, iealusel, iedsel, t3, t2, t4, t5, t6, IErt, IErs, ierd, mde
  Multiplexer #(.select(2), .width(32)) multiplexer_1 (
    .in0(ieb), .in1(f01), .in2(f10), .out(multiplexer_1_out), .sel(ForwardB));  // open: in3
  Multiplexer #(.width(5)) multiplexer_2 (.in0(IErt), .in1(ierd), .out(rdd), .sel(iedsel));
  Multiplexer #(.select(2), .width(32)) multiplexer_3 (
    .in0(iea), .in1(f01), .in2(f10), .out(multiplexer_3_out), .sel(ForwardA));  // open: in3
  Multiplexer #(.width(32)) multiplexer_4 (
    .in0(multiplexer_1_out), .in1(IEse), .out(multiplexer_4_out), .sel(iealusel));
  ALUControl alucontrol_1 (.ALUFunc(f));  // open: SHAMT, ALUop, Func
  ForwardUnit forwardunit_1 (
    .EXMrd(EMrd), .MWBrd(MWrd), .IDEXrs(IErs), .IDEXrt(IErt), .EXMregwrite(EMreW), .MWBregwrite(MWregW),
    .ForwardA(ForwardA), .ForwardB(ForwardB));
  ALU alu_1 (.Operand1(multiplexer_3_out), .Operand2(multiplexer_4_out), .ALUfunc(f), .ZF(zf), .Result(alu_1_result));
  EX2MEM ex2mem_1 (
    .NPC(ienpc), .AddrIn(alu_1_result), .ResultIn(multiplexer_4_out), .ZeroIn(zf), .RegDstIn(rdd),
    .BranchIn(t3), .MemWriteIn(t2), .MemReadIn(t4), .AdrMode(mde), .RegWriteIn(t5), .MemToRegIn(t6),
    .AddrOut(f10), .ResultOut(ex2mem_1_resultout), .RegDstOut(EMrd), .MemWriteOut(ex2mem_1_memwriteout),
    .MemReadOut(ex2mem_1_memreadout), .Mode(ex2mem_1_mode), .RegWriteOut(EMreW),
    .MemToRegOut(ex2mem_1_memtoregout));  // open: Flush, CLK, RegIn, NextPC, RegOut, ZeroOut, BranchOut
  Data data_1 (
    .Address(f10), .MemWrite(ex2mem_1_memwriteout), .MemRead(ex2mem_1_memreadout),
    .WriteData(ex2mem_1_resultout), .Mode(ex2mem_1_mode), .ReadData(data_1_readdata));  // open: CLK
  MEM2WB mem2wb_1 (
    .ResultIn(f10), .DataIn(data_1_readdata), .RegDstIn(EMrd), .RegWriteIn(EMreW),
    .MemToRegIn(ex2mem_1_memtoregout), .ResultOut(mem2wb_1_resultout), .DataOut(mem2wb_1_dataout),
    .RegDstOut(MWrd), .RegWriteOut(MWregW), .MemToRegOut(mem2wb_1_memtoregout));  // open: CLK
  Multiplexer #(.width(32)) multiplexer_5 (
    .in0(mem2wb_1_resultout), .in1(mem2wb_1_dataout), .out(f01), .sel(mem2wb_1_memtoregout));

  // Notes on the sheet:
  //   flush sv 0 salje
  //   MuxB
  //   MuxA
  //   ovo je iz alu
endmodule
